# Fritzing sketch lunsjregistrering_diagram_ (saved by Fritzing 0.9.3b)

parts:
  U1 = NodeMCU V1.0
  Part3 = RFID-RC522-v3

nets:
  N1: U1.D3, Part3.RST
  N2: U1.D4, Part3.SDA
  GND: U1.GND, Part3.GND
  N3: U1.D5, Part3.SCK
  N4: U1.D6, Part3.MISO
  N5: U1.D7, Part3.MOSI
  3V3: U1.3V3, Part3.3.3V

custom parts:
  NodeMCU V1.0: ESP8266 based NodeMCU
  RFID-RC522-v3: A simple China made RFID-RC522 Reader (6x4 cm); do check the pin labels, as this is a MFRC522 based clone.
